# Fritzing sketch Schematic (saved by Fritzing 0.9.3b)
breadboards: 1

parts:
  Componente1 = STM32F407G-DISC1
  BT1 = Bluetooth HC-06u [package=THT]
  Componente2 = Passive Buzzer  # not connected
  FC-1 = Sound Sensor  # not connected
  R2 = Photocell (LDR) [package=THT]
  Mod1 = KY-028 Digital Temperature Sensor Module [package="Breakout board"]  # not connected
  U3 = HC-SR04 [chip_label=IC package="SIP (Single Inline) [THT]"]  # not connected
  LED1 = smd LED [color="Red (633nm)" package="0603 [SMD]"]  # not connected
  R3 = Resistor [tolerance=±5% resistance=220 package="0603 [SMD]"]  # not connected
  R4 = Resistor [tolerance=±5% resistance=1k package="0603 [SMD]"]
  S1 = Pushbutton [package="[THT]"]
  J1 = Basic Servo

nets:
  N1: Componente1.pin2, Componente1.pin86, R2.pin_0
  GND: Componente1.pin3, Componente1.pin5, Componente1.pin26, Componente1.pin75, Componente1.pin76, BT1.GND, R4.Pin_1, S1.Pin_1, S1.Pin_2, J1.gnd
  N2: Componente1.pin6, J1.pulse
  N3: Componente1.pin32, R2.pin_1, R4.Pin_0
  VCC: Componente1.pin52, Componente1.pin77, BT1.VCC, S1.Pin_3, S1.Pin_4, J1.vcc
  N4: Componente1.pin73, Componente1.pin74, BT1.RXD
  N5: Componente1.pin99, BT1.TXD

custom parts:
  STM32F407G-DISC1: The STM32F4DISCOVERY Discovery kit allows users to easily develop applications with the STM32F407VG high-performance microcontroller with the Arm® Cortex®-M4 32-bit core. It includes everything required either for beginners or experienced users to get started quickly. Based on STM32F407VG, it includes an ST-LINK/V2-A embedded debug tool, one STMEMS digital accelerometer, one digital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
  Bluetooth HC-06u: Bluetooth HC-06 - face up, pins down 16.5mm x 37.5mm PCB
  KY-028 Digital Temperature Sensor Module: KY-028 Digital Temperature Sensor Module, used to measure changes in temperature.
  HC-SR04: HC-SR04 ultrasound distance sensor
